# Fritzing sketch Brunnenwassersensor_Waveshare TOF B (saved by Fritzing 0.9.10b)
breadboards: 1

parts:
  MH-ET_LIVE_ESP32_DEVKIT1 = MH-ET LIVE ESP32 DEVKIT 38 pins
  U2 = mystery part, 3 pins [chip_label=DS18B20 part_number=DS18B20]
  LED3 = LED - 5mm [color="Green (565nm)" current=0.030 package="5 mm [THT]"]
  LED4 = LED - 5mm [color="Red (633nm)" current=0.030 package="5 mm [THT]"]
  R5 = Resistor [tolerance=±5% power=0.25 resistance=220 package=THT]
  R6 = Resistor [tolerance=±5% power=0.25 resistance=330 package=THT]
  R4 = Resistor [tolerance=±5% power=0.25 resistance=4.7k package=THT]
  LED5 = LED - 5mm [color="Yellow (595nm)" current=0.030 package="5 mm [THT]"]
  R7 = Resistor [tolerance=±5% power=0.25 resistance=220 package=THT]
  Bauteil1 = I2C level shifter bidirectional
  J6 = male pin header, 4 pins [form="♂ (male)"]

nets:
  N1: MH-ET_LIVE_ESP32_DEVKIT1.3V3, U2.pin3, R4.Pin_1
  N2: MH-ET_LIVE_ESP32_DEVKIT1.IO25, U2.pin2, R4.Pin_0
  N3: MH-ET_LIVE_ESP32_DEVKIT1.5V, Bauteil1.HV, J6.pin1
  N4: MH-ET_LIVE_ESP32_DEVKIT1.GND#64, U2.pin1, LED3.cathode, LED4.cathode, LED5.cathode, Bauteil1.GND, J6.pin2
  N5: MH-ET_LIVE_ESP32_DEVKIT1.IO23, R5.Pin_0
  N6: MH-ET_LIVE_ESP32_DEVKIT1.IO22, Bauteil1.LV1
  N7: MH-ET_LIVE_ESP32_DEVKIT1.IO21, Bauteil1.LV2
  N8: MH-ET_LIVE_ESP32_DEVKIT1.IO19, R6.Pin_0
  N9: MH-ET_LIVE_ESP32_DEVKIT1.IO4, R7.Pin_0
  N10: LED3.anode, R6.Pin_1
  N11: LED4.anode, R5.Pin_1
  N12: LED5.anode, R7.Pin_1
  N13: Bauteil1.HV1, J6.pin4
  N14: Bauteil1.HV2, J6.pin3

notes:
  Verbindung zum Waveshare TOF Laser Range Sensor (B)
  [VDD | GND | sda | scl ]

custom parts:
  MH-ET LIVE ESP32 DEVKIT 38 pins: http://mh.nodebb.com/topic/2/mh-et-live-esp32-devkit
